// Logisim project 6-2.circ as structural Verilog: 5 circuits, main circuit main
module main (
  input  Load,
  input  Reset,
  input  I3,
  input  I2,
  input  I1,
  input  I0
);

  wire and_1_out, and_2_out, and_3_out, and_4_out, and_5_out, and_6_out, and_7_out, and_8_out, clock_1_out,
       or_1_out, or_2_out, or_3_out, or_4_out;

  Clock clock_1 (.out(clock_1_out));
  // AND_Gate and_1 has open pins: out=and_1_out
  // AND_Gate and_2 has open pins: out=and_2_out
  // AND_Gate and_3 has open pins: out=and_3_out
  // AND_Gate and_4 has open pins: out=and_4_out
  // AND_Gate and_5 has open pins: out=and_5_out
  // AND_Gate and_6 has open pins: out=and_6_out
  // AND_Gate and_7 has open pins: out=and_7_out
  // AND_Gate and_8 has open pins: out=and_8_out
  or or_1 (or_1_out, and_1_out, and_2_out);
  or or_2 (or_2_out, and_3_out, and_4_out);
  or or_3 (or_3_out, and_5_out, and_6_out);
  or or_4 (or_4_out, and_7_out, and_8_out);
  D_Flip_Flop d_flip_flop_1 (.in_1(or_1_out), .in_2(clock_1_out), .in_3(1'b0));  // open: out_4
  D_Flip_Flop d_flip_flop_2 (.in_1(or_2_out), .in_2(clock_1_out), .in_3(1'b0));  // open: out_4
  D_Flip_Flop d_flip_flop_3 (.in_1(or_3_out), .in_2(clock_1_out), .in_3(1'b0));  // open: out_4
  D_Flip_Flop d_flip_flop_4 (.in_1(or_4_out), .in_2(clock_1_out), .in_3(1'b0));  // open: out_4

  // Notes on the sheet:
  //   Logic diagram for exercise 6-2
  //   Clk
endmodule

module _8X1_MUX (
  input  in_1,
  input  in_2,
  input  in_3,
  input  in_4,
  input  in_5,
  input  in_6,
  input  in_7,
  input  in_8,
  input  in_9,
  input  in_10,
  input  in_11,
  output out_12
);
endmodule

module _2X1_MUL (
  input  in_1,
  input  in_2,
  input  in_3,
  output out_4
);
endmodule

module _4X1_MUX (
  input  in_1,
  input  in_2,
  input  in_3,
  input  in_4,
  input  in_5,
  input  in_6,
  output out_7
);
endmodule

module D_Flip_Flop (
  input  in_1,
  input  in_2,
  input  in_3,
  output out_4
);
endmodule
