// Logisim project 6-25.circ as structural Verilog: 1 circuit, main circuit main
module main (
  input  Shift,
  input  Clear,
  input  Load,
  input  [5:0] Init_Value,
  output [5:0] out_5
);

  wire Clk_out, shift_register_1_out;

  Clock Clk (.out(Clk_out));
  Multiplexer multiplexer_1 ();  // open: in0, in1, out, sel, en
  Shift_Register #(.length(6)) shift_register_1 (
    .shift(Shift), .in(shift_register_1_out), .clk(Clk_out), .out(shift_register_1_out), .load(Load),
    .clr(Clear), .d0(Init_Value[0]), .q0(out_5[0]), .d1(Init_Value[1]), .q1(out_5[1]), .d2(Init_Value[2]),
    .q2(out_5[2]), .d3(Init_Value[3]), .q3(out_5[3]), .d4(Init_Value[4]), .q4(out_5[4]), .d5(Init_Value[5]),
    .q5(out_5[5]));
  Counter #(.width(6), .max('h3f)) counter_1 ();  // open: load, D, count, Q, carry, clk, clr
endmodule
