// Logisim project 6-29.circ as structural Verilog
module switch_tail_counter (
  input  reset,
  output out_2,
  output out_3,
  output out_4,
  output out_5
);

  wire Clk_out, d_ff_4_qn;

  Clock Clk (.out(Clk_out));
  D_Flip_Flop d_ff_1 (.clk(Clk_out), .D(d_ff_4_qn), .Q(out_2), .preset(1'b0), .en(1'b1), .reset(reset));  // open: Qn
  D_Flip_Flop d_ff_2 (.clk(Clk_out), .D(out_2), .Q(out_3), .preset(1'b0), .en(1'b1), .reset(reset));  // open: Qn
  D_Flip_Flop d_ff_3 (.clk(Clk_out), .D(out_3), .Q(out_4), .preset(1'b0), .en(1'b1), .reset(reset));  // open: Qn
  D_Flip_Flop d_ff_4 (.clk(Clk_out), .D(out_4), .Q(out_5), .Qn(d_ff_4_qn), .preset(1'b0), .en(1'b1), .reset(reset));

  // Notes on the sheet:
  //   Switch Tail Counter
endmodule
